# Fritzing sketch Orologio DS3231 (saved by Fritzing 0.9.3b)

parts:
  ZS-042_RTC1 = ZS-042 RTC Module
  U2 = LCD-16X2 [package=lcd-16x2]  # not connected
  Componente1 = Arduino Uno (Rev3)
  ZS-042_RTC2 = ZS-042 RTC Module

nets:
  GND: ZS-042_RTC1.GND, Componente1.GND
  VCC: ZS-042_RTC1.VCC, Componente1.5V
  N1: ZS-042_RTC1.SDA, Componente1.A4/SDA, ZS-042_RTC2.SDA
  N2: ZS-042_RTC1.SCL, Componente1.A5/SCL, ZS-042_RTC2.SCL
  3V3: Componente1.3V3, ZS-042_RTC2.VCC

// code stored in the sketch: Orologio DS3231.ino
#include <DS3232RTC.h>
#include <TimeLib.h>
#include <Wire.h>
#include <LiquidCrystal.h>

LiquidCrystal lcd(12, 11, 5, 4, 3, 2);

time_t t;
tmElements_t tm;

float temperatura = 0; 
float temp1 = 0; 
int digits = 0;
char tabmesi [37] = "genfebmaraprmaggiulugagosetottnovdic"; 
int mese = 0; 
int lavoro = 0; 

void esponidati(void)
{
  
  lcd.clear();
  lcd.setCursor(0, 0);
  lcd.print(" ");
  lcd.print(day());
  lcd.print(' ');
  mese = month();
  mese = mese - 1; 
  lcd.print (tabmesi [(mese * 3)]); 
  lcd.print (tabmesi [(mese * 3 + 1)]); 
  lcd.print (tabmesi [(mese * 3 + 2)]); 
  lcd.print(' ');
  lcd.print(year());
  lcd.setCursor(0, 1);
  lcd.print(hour());
  digits = (minute());
  printDigits(); 
  digits = (second());
  printDigits(); 
  lcd.print (" t:");
  lcd.print (temp1);
}

void printDigits()
{
  lcd.print(':');
  if (digits < 10)
    lcd.print('0');
  lcd.print(digits);
}
void setup(void)
{
  Serial.begin (9600); 
  lcd.begin(16, 2); 
  lcd.print ("Buongiorno"); 
  delay (1500);
  lcd.clear ();
  lcd.setCursor(0, 0); 
  setSyncProvider(RTC.get); 
  lcd. clear ();
  if (timeStatus() != timeSet) 
    lcd.print("Orologio non"); 
  else
    lcd.print("Orologio"); 
  lcd.setCursor (0, 1);
  lcd.print ("sincronizzato"); 
  delay (1500);
  temperatura = RTC.temperature(); 
}
void loop(void)
{
  if (Serial.available() == 17) 
  { 
    int y = Serial.parseInt();
    tm.Year = y2kYearToTm(y);
    tm.Month = Serial.parseInt();
    tm.Day = Serial.parseInt();
    tm.Hour = Serial.parseInt();
    tm.Minute = Serial.parseInt();
    tm.Second = Serial.parseInt();
    t = makeTime(tm);
    RTC.set(t); 
    setTime(t); 
  } 
  digits = (second()); 
  lavoro = digits % 10;
  if (lavoro == 9) 
    temperatura = RTC.temperature(); 
  temp1 = temperatura / 4.0;
  esponidati(); 
  delay (1000); 
}
